# Fritzing sketch freemcom (saved by Fritzing 0.8.5b)
breadboards: 1

parts:
  arduino = Arduino Uno (Rev3)
  Start/Stop = Pushbutton [package="[THT]"]
  R1 = Resistor [tolerance=±5% resistance=10k package=THT]
  LED1_(for_12V) = LED - 5mm [color="Red (633nm)" package="5 mm [THT]"]
  J2 = Relay [part_number=SLD01101P package=THT]
  Buzzer(12V) = Piezo Speaker
  Reset = Pushbutton [package="[THT]"]
  Fuse1 = Fuse with Handler [part_number=10A]
  J1 = Relay [part_number=SLD01101P package=THT]

nets (from the schematic view):
  N1: arduino.D2, Start/Stop.Pin_1, Start/Stop.Pin_2, R1.Pin_0
  N2: arduino.D6_PWM, J2.COIL1
  N3: arduino.D7, J1.COIL1
  N4: arduino.RESET, Reset.Pin_3, Reset.Pin_4
  N5: arduino.5V, Start/Stop.Pin_3, Start/Stop.Pin_4
  GND: arduino.GND, R1.Pin_1, LED1_(for_12V).cathode, J2.COIL2, Reset.Pin_1, Reset.Pin_2, J1.COIL2
  5V: arduino.VIN
  N6: LED1_(for_12V).anode, J2.C1, J2.C2
  N7: J2.A, Fuse1.Connector2, J1.A
  N8: Buzzer(12V).pin2, J1.C1, J1.C2
  12V: Fuse1.Connector1

notes:
  COM1
  COM2
  NO1
  NO2
